# Fritzing sketch sensorboard3 (saved by Fritzing 0.6.5b)
breadboards: 1

parts:
  U2 = Arduino Mega
  パーツ2 = Logic Level Converter
  BMA2 = BMA180_Breakout
  R3 = Resistor [tolerance=±10% resistance=1.8k package=THT]
  R4 = Resistor [tolerance=±10% resistance=3.3k package=THT]
  GPS1 = Gms_u1LP
  RTC3 = RX_8803
  C1 = Ceramic Capacitor [capacitance=100nF package="100 mil [THT, multilayer]"]

nets:
  N1: U2.3V3, パーツ2.LV, BMA2.connector8, BMA2.connector12, BMA2.connector15, GPS1.connector0, GPS1.connector3, GPS1.connector19, RTC3.connector5, C1.1
  N2: U2.+5V, パーツ2.HV
  GND: U2.GND, パーツ2.GND, BMA2.connector10, BMA2.connector14, R4.Pin_1, GPS1.connector2, GPS1.connector7, GPS1.connector11, GPS1.connector18, RTC3.connector6, RTC3.connector10, C1.0
  N3: U2.D18, R3.Pin_1
  N4: U2.D19, GPS1.connector8
  N5: U2.D20, パーツ2.TX_HV
  N6: U2.D21, パーツ2.TX2_HV
  N7: U2.D24, GPS1.connector12
  N8: U2.D26, RTC3.connector8
  N9: パーツ2.TX2_LV, BMA2.connector11, RTC3.connector1
  N10: パーツ2.TX_LV, BMA2.connector9, RTC3.connector12
  N11: R3.Pin_0, R4.Pin_0, GPS1.connector9
